# Fritzing sketch 8_Digital_Inputs_NRF24-230 (saved by Fritzing 0.9.3b)
circuit board: 5cm x 8.2cm
breadboards: 1

parts:
  J5 = female pin header, 3 pins [form="♀ (female)"]
  J6 = female pin header, 6 pins [form="♀ (female)"]
  J7 = female pin header, 3 pins [form="♀ (female)"]
  R3 = Resistor [tolerance=±5% resistance=1k part_number=1K package=THT]
  C1 = Ceramic Capacitor [capacitance=0.1µF voltage=10V package="100 mil [THT, multilayer]"]
  R2 = Resistor [tolerance=±5% resistance=4.7k part_number=3K-6K package=THT]
  R57 = Resistor [tolerance=±5% resistance=4.7k package=THT]
  J8 = screw terminal, 9 pins
  D27 = Rectifier Diode [part_number=1N4001 breakdown_voltage=3.6V package="300 mil [THT]"]
  D28 = Rectifier Diode [part_number=1N4001 package="300 mil [THT]"]
  D29 = Rectifier Diode [part_number=1N4001 package="300 mil [THT]"]
  D30 = Rectifier Diode [part_number=1N4001 package="300 mil [THT]"]
  D31 = Rectifier Diode [part_number=1N4001 package="300 mil [THT]"]
  D32 = Rectifier Diode [part_number=1N4001 package="300 mil [THT]"]
  D33 = Rectifier Diode [part_number=1N4001 package="300 mil [THT]"]
  D34 = Rectifier Diode [part_number=1N4001 package="300 mil [THT]"]
  J9 = female pin header, 9 pins [form="♀ (female)" part_number="10K Array"]
  IC6 = IC, DIP package, 16 pins [chip_label=CD4014]
  Componente1 = NRF24L01+ Breakout Board
  C8 = Electrolytic Capacitor [capacitance=560µF package="200 mil [THT, electrolytic]"]
  HLK-PM4 = HLK-PM01 [part_number=5V]
  J11 = Screw terminal - 2 pins [package=THT]

nets:
  N1: J5.pin2, J7.pin3, C1.1, J8.pin1, IC6.pin8, Componente1.GND, C8.-, HLK-PM4.-Vo
  N2: J5.pin3, J7.pin1, R57.Pin_1, J9.pin1, IC6.pin16, C8.+, HLK-PM4.+Vo
  N3: J6.pin1, R2.Pin_0, Componente1.MOSI
  N4: J6.pin3, R3.Pin_0, Componente1.SCK
  N5: J6.pin4, IC6.pin9
  N6: J6.pin5, IC6.pin10
  N7: J6.pin6, IC6.pin3
  N8: J7.pin2, Componente1.VCC
  N9: R3.Pin_1, C1.0, Componente1.CE, Componente1.CS
  N10: R2.Pin_1, Componente1.MISO
  N11: R57.Pin_0, IC6.pin11
  N12: J8.pin2, D27.cathode
  N13: J8.pin3, D28.cathode
  N14: J8.pin4, D29.cathode
  N15: J8.pin5, D30.cathode
  N16: J8.pin6, D31.cathode
  N17: J8.pin7, D32.cathode
  N18: J8.pin8, D33.cathode
  N19: J8.pin9, D34.cathode
  N20: D27.anode, J9.pin9, IC6.pin1
  N21: D28.anode, J9.pin8, IC6.pin15
  N22: D29.anode, J9.pin7, IC6.pin14
  N23: D30.anode, J9.pin6, IC6.pin13
  N24: D31.anode, J9.pin5, IC6.pin4
  N25: D32.anode, J9.pin4, IC6.pin5
  N26: D33.anode, J9.pin3, IC6.pin6
  N27: D34.anode, J9.pin2, IC6.pin7
  N28: HLK-PM4.AC#0, J11.pin1
  N29: HLK-PM4.AC#1, J11.pin2

notes:
  GND OUT IN
  3
  1
  2
  4
  5
  6
  7
  8
  GND
  8 IN - NRF24
  v1.1
  CD4014
  OJO!! 230V AC
  230V
