# Fritzing sketch Analog_Input-DS18B20_NRF24-230 (saved by Fritzing 0.9.3b)
circuit board: 5cm x 5cm
breadboards: 1

parts:
  J5 = female pin header, 3 pins [form="♀ (female)"]
  J6 = female pin header, 6 pins [form="♀ (female)"]
  R1 = Resistor [tolerance=±5% resistance=2.2M package=THT]
  J7 = female pin header, 3 pins [form="♀ (female)"]
  R3 = Resistor [tolerance=±5% resistance=1k part_number=1K package=THT]
  C1 = Ceramic Capacitor [capacitance=0.1µF voltage=10V part_number=104 package="100 mil [THT, multilayer]"]
  R2 = Resistor [tolerance=±5% resistance=4.7k part_number=3K-6K package=THT]
  J4 = screw terminal, 3 pins
  Componente1 = NRF24L01+ Breakout Board
  C7 = Electrolytic Capacitor [capacitance=560µF package="200 mil [THT, electrolytic]"]
  HLK-PM3 = HLK-PM01 [part_number=5V]
  J10 = Screw terminal - 2 pins [package=THT]
  R4 = Resistor [tolerance=±5% resistance=220 package=THT]

nets:
  N1: J5.pin2, R1.Pin_1, J7.pin3, C1.1, J4.pin1, Componente1.GND, C7.-, HLK-PM3.-Vo
  N2: J5.pin3, J7.pin1, J4.pin3, C7.+, HLK-PM3.+Vo, R4.Pin_1
  N3: J6.pin1, R2.Pin_0, Componente1.MOSI
  N4: J6.pin3, R3.Pin_0, Componente1.SCK
  N5: J6.pin6, R1.Pin_0, J4.pin2, R4.Pin_0
  N6: J7.pin2, Componente1.VCC
  N7: R3.Pin_1, C1.0, Componente1.CE, Componente1.CS
  N8: R2.Pin_1, Componente1.MISO
  N9: HLK-PM3.AC#0, J10.pin1
  N10: HLK-PM3.AC#1, J10.pin2

notes:
  -   s   +
  GND OUT IN
  V1.1
  OJO!! 230V AC
  230V
  R4-Pull Up (OneWire)
  R1-Pull Down (Analog)
