# Fritzing sketch Analog_Input-DS18B20_NRF24 (saved by Fritzing 0.9.3b)
circuit board: 5cm x 3cm
breadboards: 1

parts:
  J5 = female pin header, 3 pins [form="♀ (female)"]
  J6 = female pin header, 6 pins [form="♀ (female)"]
  D1 = Rectifier Diode [part_number=1N4001 package="300 mil [THT]"]
  R1 = Resistor [tolerance=±5% resistance=2.2M package=THT]
  J1 = screw terminal, 2 pins
  J7 = female pin header, 3 pins [form="♀ (female)"]
  R3 = Resistor [tolerance=±5% resistance=1k part_number=1K package=THT]
  C1 = Ceramic Capacitor [capacitance=0.1µF voltage=10V part_number=104 package="100 mil [THT, multilayer]"]
  R2 = Resistor [tolerance=±5% resistance=4.7k part_number=3K-6K package=THT]
  J4 = screw terminal, 3 pins
  Componente1 = NRF24L01+ Breakout Board
  R4 = Resistor [tolerance=±5% resistance=4.7k package=THT]

nets:
  N1: J5.pin1, D1.cathode
  N2: J5.pin2, R1.Pin_1, J1.pin1, J7.pin3, C1.1, J4.pin1, Componente1.GND
  N3: J5.pin3, J7.pin1, J4.pin3, R4.Pin_1
  N4: J6.pin1, R2.Pin_0, Componente1.MOSI
  N5: J6.pin3, R3.Pin_0, Componente1.SCK
  N6: J6.pin6, R1.Pin_0, J4.pin2, R4.Pin_0
  N7: D1.anode, J1.pin2
  N8: J7.pin2, Componente1.VCC
  N9: R3.Pin_1, C1.0, Componente1.CE, Componente1.CS
  N10: R2.Pin_1, Componente1.MISO

notes:
  -   s   +
  GND OUT IN
  - +
  6-20DC
  V1.1
  R1-Pull Down (Analog)
  R4-Pull Up (OneWire)
